// Digital circuit es.1.dig as structural Verilog
module es_1 (
  input  X0,
  input  X1,
  input  X2,
  input  X3,
  input  X4,
  output U
);

  wire nand_1_out, nand_2_out, nand_3_out, nand_4_out, nand_5_out, nand_6_out, not_1_out, not_2_out,
       not_3_out, not_4_out, not_5_out;

  not not_1 (not_1_out, X0);
  not not_2 (not_2_out, X1);
  not not_3 (not_3_out, X2);
  not not_4 (not_4_out, X3);
  not not_5 (not_5_out, X4);
  nand nand_1 (nand_1_out, not_2_out, not_1_out, X2);
  nand nand_2 (nand_2_out, X3, not_2_out, X0);
  nand nand_3 (nand_3_out, not_4_out, X0, X1, X2);
  nand nand_4 (nand_4_out, X3, X1, not_5_out);
  nand nand_5 (nand_5_out, not_3_out, X4);
  nand nand_6 (nand_6_out, X3, not_1_out, X4);
  nand nand_7 (U, nand_1_out, nand_2_out, nand_3_out, nand_4_out, nand_5_out, nand_6_out);
endmodule
