// Digital circuit es. 4.dig as structural Verilog
module es__4 (
  input  a0,
  input  b0,
  input  r0,
  input  a1,
  input  b1,
  input  a2,
  input  b2,
  input  a3,
  input  b3,
  input  a4,
  input  b4,
  output s0,
  output s1,
  output s2,
  output s3,
  output s4,
  output r1
);

  wire and_1_out, and_2_out, and_3_out, and_4_out, and_5_out, and_6_out, and_7_out, and_8_out, and_9_out,
       and_10_out, or_1_out, or_2_out, or_3_out, or_4_out, xor_1_out, xor_2_out, xor_4_out, xor_5_out,
       xor_7_out, xor_8_out, xor_10_out, xor_11_out, xor_13_out, xor_14_out;

  xor xor_1 (xor_1_out, a0, b0);
  and and_1 (and_1_out, a0, b0);
  xor xor_2 (xor_2_out, a0, b0);
  xor xor_3 (s0, r0, xor_1_out);
  and and_2 (and_2_out, r0, xor_2_out);
  or or_1 (or_1_out, and_1_out, and_2_out);
  xor xor_4 (xor_4_out, a1, b1);
  and and_3 (and_3_out, a1, b1);
  xor xor_5 (xor_5_out, a1, b1);
  xor xor_6 (s1, or_1_out, xor_4_out);
  and and_4 (and_4_out, or_1_out, xor_5_out);
  or or_2 (or_2_out, and_3_out, and_4_out);
  xor xor_7 (xor_7_out, a2, b2);
  and and_5 (and_5_out, a2, b2);
  xor xor_8 (xor_8_out, a2, b2);
  xor xor_9 (s2, or_2_out, xor_7_out);
  and and_6 (and_6_out, or_2_out, xor_8_out);
  or or_3 (or_3_out, and_5_out, and_6_out);
  xor xor_10 (xor_10_out, a3, b3);
  and and_7 (and_7_out, a3, b3);
  xor xor_11 (xor_11_out, a3, b3);
  xor xor_12 (s3, or_3_out, xor_10_out);
  and and_8 (and_8_out, or_3_out, xor_11_out);
  or or_4 (or_4_out, and_7_out, and_8_out);
  xor xor_13 (xor_13_out, a4, b4);
  and and_9 (and_9_out, a4, b4);
  xor xor_14 (xor_14_out, a4, b4);
  xor xor_15 (s4, or_4_out, xor_13_out);
  and and_10 (and_10_out, or_4_out, xor_14_out);
  or or_5 (r1, and_9_out, and_10_out);
endmodule
