// Digital circuit es.1 porta.dig as structural Verilog
module es_1_porta (
  input  p1,
  input  p2,
  input  s,
  output v,
  output r
);

  wire and_1_out, and_2_out, and_3_out, not_1_out, not_2_out;

  not not_1 (not_1_out, p1);
  not not_2 (not_2_out, p2);
  and and_1 (and_1_out, p1, not_2_out);
  and and_2 (and_2_out, not_1_out, p2);
  and and_3 (and_3_out, s, p2, p1);
  or or_1 (v, and_1_out, and_2_out, and_3_out);
  not not_3 (r, v);
endmodule
